// Logisim project 8majlogisim.circ as structural Verilog: 7 circuits, main circuit main
module main (
  input  in_1,
  output [3:0] out_2,
  output [3:0] out_3
);

  wire and_1_out, and_2_out, clock_1_out, not_1_out;

  and and_1 (and_1_out, clock_1_out, not_1_out);
  Clock clock_1 (.out(clock_1_out));
  Counter #(.width(4), .max('hf)) counter_1 (.Q(out_2), .clk(and_1_out), .clr(in_1));  // open: load, D, count, carry
  not not_1 (not_1_out, in_1);
  Counter #(.width(4), .max('hf)) counter_2 (
    .Q(out_3), .clk(and_2_out), .clr(not_1_out));  // open: load, D, count, carry
  and and_2 (and_2_out, clock_1_out, in_1);
endmodule

module Comparator (
  input  [3:0] in_1,
  input  [3:0] in_2,
  output out_3
);

  wire clock_1_out, comparator_1_gt, comparator_2_eq;
  wire [3:0] register_1_q;

  Clock clock_1 (.out(clock_1_out));
  Register #(.width(4)) register_1 (.D(in_1), .Q(register_1_q), .clk(clock_1_out));  // open: en, clr
  and and_1 (out_3, comparator_1_gt, comparator_2_eq);
  Comparator_part #(.width(4)) comparator_1 (.a(register_1_q), .b(4'b0110), .gt(comparator_1_gt));  // open: eq, lt
  Comparator_part #(.width(4)) comparator_2 (.a(4'b0001), .b(in_2), .eq(comparator_2_eq));  // open: gt, lt
endmodule

module Hela_kretsen_ful (
  input  in_1,
  output dash,
  output _7,
  output _3,
  output _1,
  output dot
);

  wire [3:0] main_1_out_2, main_1_out_3;

  Pause_comparator pause_comparator_1 (.out_2(_7), .\mellan_bokstäver (_3), .out_4(_1), .in_1(main_1_out_2));
  main main_1 (.in_1(in_1), .out_2(main_1_out_2), .out_3(main_1_out_3));
  Dash_dot_comparator dash_dot_comparator_1 (.dash(dash), .dot(dot), .in_1(main_1_out_3));
endmodule

module Dash_dot_comparator (
  input  [3:0] in_1,
  output dot,
  output dash
);

  wire clock_1_out, comparator_1_eq, comparator_1_gt, comparator_1_lt, comparator_2_eq, comparator_3_eq,
       not_1_out, or_1_out;
  wire [3:0] register_1_q;

  Clock clock_1 (.out(clock_1_out));
  Register #(.width(4)) register_1 (.D(in_1), .Q(register_1_q), .clk(clock_1_out));  // open: en, clr
  and and_1 (dash, comparator_1_gt, comparator_2_eq);
  Comparator_part #(.width(4), .mode("unsigned")) comparator_1 (
    .a(register_1_q), .b(4'b0010), .gt(comparator_1_gt), .eq(comparator_1_eq), .lt(comparator_1_lt));
  Comparator_part #(.width(4)) comparator_2 (.a(4'b0000), .b(in_1), .eq(comparator_2_eq));  // open: gt, lt
  Comparator_part #(.width(4), .mode("unsigned")) comparator_3 (
    .a(register_1_q), .b(4'b0000), .eq(comparator_3_eq));  // open: gt, lt
  and and_2 (dot, comparator_2_eq, not_1_out, or_1_out);
  not not_1 (not_1_out, comparator_3_eq);
  or or_1 (or_1_out, comparator_1_eq, comparator_1_lt);
endmodule

module Pause_comparator (
  input  [3:0] in_1,
  output out_2,
  output \mellan_bokstäver ,
  output out_4
);

  wire clock_1_out, comparator_1_eq, comparator_1_gt, comparator_1_lt, comparator_2_eq, comparator_2_gt,
       comparator_2_lt, comparator_3_eq, comparator_4_eq, not_1_out, or_1_out, or_2_out;
  wire [3:0] register_1_q;

  Clock clock_1 (.out(clock_1_out));
  Comparator_part #(.width(4), .mode("unsigned")) comparator_1 (
    .a(register_1_q), .b(4'b0101), .gt(comparator_1_gt), .eq(comparator_1_eq), .lt(comparator_1_lt));
  Register #(.width(4)) register_1 (.D(in_1), .Q(register_1_q), .clk(clock_1_out));  // open: en, clr
  and and_1 (out_2, comparator_1_gt, comparator_3_eq);
  Comparator_part #(.width(4), .mode("unsigned")) comparator_2 (
    .a(register_1_q), .b(4'b0010), .gt(comparator_2_gt), .eq(comparator_2_eq), .lt(comparator_2_lt));
  or or_1 (or_1_out, comparator_1_eq, comparator_1_lt);
  Comparator_part #(.width(4)) comparator_3 (.a(4'b0000), .b(in_1), .eq(comparator_3_eq));  // open: gt, lt
  and and_2 (\mellan_bokstäver , comparator_2_gt, or_1_out, comparator_3_eq);
  and and_3 (out_4, comparator_3_eq, not_1_out, or_2_out);
  Comparator_part #(.width(4), .mode("unsigned")) comparator_4 (
    .a(register_1_q), .b(4'b0000), .eq(comparator_4_eq));  // open: gt, lt
  not not_1 (not_1_out, comparator_4_eq);
  or or_2 (or_2_out, comparator_2_eq, comparator_2_lt);

  // Notes on the sheet:
  //   mellanslag
  //   mellan delar av en bokstav
endmodule

module Send_to_Arduino (
  input  _7,
  input  _3,
  input  _1,
  input  dash,
  input  dot,
  output out_6,
  output out_7,
  output out_8,
  output out_9,
  output Send,
  output out_11,
  output out_12
);

  wire multiplexer_1_out, multiplexer_2_out;
  wire [1:0] counter_1_q;

  or or_1 (Send, _7, _3);
  Counter #(.width(2), .max('h3)) counter_1 (.Q(counter_1_q), .clk(_1), .clr(Send));  // open: load, D, count, carry
  D_Flip_Flop x0 (.clk(_1), .D(dash), .Q(out_6));  // open: Qn, preset, en, reset
  D_Flip_Flop x1 (.clk(_1), .D(out_6), .Q(out_7));  // open: Qn, preset, en, reset
  D_Flip_Flop x2 (.clk(_1), .D(out_7), .Q(out_8));  // open: Qn, preset, en, reset
  D_Flip_Flop x3 (.clk(_1), .D(out_8), .Q(out_9));  // open: Qn, preset, en, reset
  Multiplexer #(.select(2)) multiplexer_1 (
    .in0(1'b0), .in1(1'b0), .in2(1'b1), .in3(1'b1), .out(multiplexer_1_out), .sel(counter_1_q));  // open: en
  Multiplexer #(.select(2)) multiplexer_2 (
    .in0(1'b0), .in1(1'b1), .in2(1'b0), .in3(1'b1), .out(multiplexer_2_out), .sel(counter_1_q));  // open: en
  D_Flip_Flop x4 (.clk(_1), .D(multiplexer_1_out), .Q(out_11));  // open: Qn, preset, en, reset
  D_Flip_Flop x6 (.clk(_1), .D(multiplexer_2_out), .Q(out_12));  // open: Qn, preset, en, reset

  // Notes on the sheet:
  //   morsekod till arduinon
endmodule

module Numbers_mkt_kretsar (
  output x0_out,
  output x1_out,
  output x2_out,
  output x3_out,
  output x4_out,
  output Send,
  output c2_out,
  output c1_out,
  output c0__out
);

  wire and_1_out, button_1_out, d_ff_1_q, d_ff_2_q, d_ff_3_q, hela_kretsen_ful_1__1, hela_kretsen_ful_1__3,
       hela_kretsen_ful_1__7, hela_kretsen_ful_1_dash, hela_kretsen_ful_1_dot, multiplexer_1_out,
       multiplexer_2_out, multiplexer_3_out, not_1_out, or_1_out, or_3_out, or_4_out, or_5_out;
  wire [2:0] counter_1_q;

  or or_1 (or_1_out, hela_kretsen_ful_1_dot, hela_kretsen_ful_1_dash, hela_kretsen_ful_1__1, hela_kretsen_ful_1__3, hela_kretsen_ful_1__7);
  Button button_1 (.out(button_1_out));
  or or_2 (Send, hela_kretsen_ful_1__7, hela_kretsen_ful_1__3);
  Hela_kretsen_ful hela_kretsen_ful_1 (
    .in_1(button_1_out), ._7(hela_kretsen_ful_1__7), ._3(hela_kretsen_ful_1__3), ._1(hela_kretsen_ful_1__1),
    .dash(hela_kretsen_ful_1_dash), .dot(hela_kretsen_ful_1_dot));
  or or_3 (or_3_out, hela_kretsen_ful_1_dot, hela_kretsen_ful_1_dash);
  Clock clock_1 ();  // open: out
  D_Flip_Flop d_ff_1 (.clk(or_3_out), .D(hela_kretsen_ful_1_dash), .Q(d_ff_1_q));  // open: Qn, preset, en, reset
  or or_4 (or_4_out, Send, or_5_out);
  or or_5 (or_5_out, Send, hela_kretsen_ful_1__1);
  D_Flip_Flop d_ff_2 (.clk(or_1_out), .D(Send), .Q(d_ff_2_q), .reset(and_1_out));  // open: Qn, preset, en
  not not_1 (not_1_out, d_ff_2_q);
  and and_1 (and_1_out, not_1_out, d_ff_3_q);
  D_Flip_Flop d_ff_3 (.clk(or_1_out), .D(d_ff_2_q), .Q(d_ff_3_q), .reset(and_1_out));  // open: Qn, preset, en
  Counter #(.width(3), .max('h4)) counter_1 (
    .Q(counter_1_q), .clk(or_5_out), .clr(and_1_out));  // open: load, D, count, carry
  D_Flip_Flop x0 (.clk(or_4_out), .D(d_ff_1_q), .Q(x0_out), .reset(and_1_out));  // open: Qn, preset, en
  D_Flip_Flop x1 (.clk(or_4_out), .D(x0_out), .Q(x1_out), .reset(and_1_out));  // open: Qn, preset, en
  D_Flip_Flop x2 (.clk(or_4_out), .D(x1_out), .Q(x2_out), .reset(and_1_out));  // open: Qn, preset, en
  D_Flip_Flop x3 (.clk(or_4_out), .D(x2_out), .Q(x3_out), .reset(and_1_out));  // open: Qn, preset, en
  D_Flip_Flop x4 (.clk(or_4_out), .D(x3_out), .Q(x4_out), .reset(and_1_out));  // open: Qn, preset, en
  Multiplexer #(.select(3)) multiplexer_1 (
    .in0(1'b0), .in1(1'b0), .in2(1'b0), .in3(1'b0), .in4(1'b1), .in5(1'b1), .out(multiplexer_1_out),
    .sel(counter_1_q));  // open: in6, in7, en
  Multiplexer #(.select(3)) multiplexer_2 (
    .in0(1'b0), .in1(1'b0), .in2(1'b1), .in3(1'b1), .in4(1'b0), .out(multiplexer_2_out), .sel(counter_1_q));  // open: in5, in6, in7, en
  Multiplexer #(.select(3)) multiplexer_3 (
    .in0(1'b0), .in1(1'b1), .in2(1'b0), .in3(1'b1), .in4(1'b0), .out(multiplexer_3_out), .sel(counter_1_q));  // open: in5, in6, in7, en
  D_Flip_Flop c2 (.clk(or_5_out), .D(multiplexer_1_out), .Q(c2_out), .reset(and_1_out));  // open: Qn, preset, en
  D_Flip_Flop c1 (.clk(or_5_out), .D(multiplexer_2_out), .Q(c1_out), .reset(and_1_out));  // open: Qn, preset, en
  D_Flip_Flop c0 (.clk(or_5_out), .D(multiplexer_3_out), .Q(c0__out), .reset(and_1_out));  // open: Qn, preset, en

  // Notes on the sheet:
  //   morsekod till arduinon
endmodule
