// Logisim project Counter.circ as structural Verilog: 1 circuit, main circuit main
module main (
  output [7:0] out_1,
  output [7:0] out_2
);

  wire and_1_out, and_2_out, button_1_out, clock_1_out, not_1_out;

  and and_1 (and_1_out, clock_1_out, not_1_out);
  Button button_1 (.out(button_1_out));
  Clock clock_1 (.out(clock_1_out));
  Counter counter_1 (.Q(out_1), .clk(and_1_out), .clr(button_1_out));  // open: load, D, count, carry
  not not_1 (not_1_out, button_1_out);
  Counter counter_2 (.Q(out_2), .clk(and_2_out), .clr(not_1_out));  // open: load, D, count, carry
  and and_2 (and_2_out, clock_1_out, button_1_out);
endmodule
