// Logisim project Gammalt.circ as structural Verilog: 2 circuits, main circuit Send to Arduino
module Send_to_Arduino (
  input  _7,
  input  _3,
  input  _1,
  input  dash,
  input  dot,
  output out_6,
  output out_7,
  output out_8,
  output out_9,
  output Send,
  output out_11,
  output out_12
);

  wire multiplexer_1_out, multiplexer_2_out;
  wire [1:0] counter_1_q;

  or or_1 (Send, _7, _3);
  Counter #(.width(2), .max('h3)) counter_1 (.Q(counter_1_q), .clk(_1), .clr(Send));  // open: load, D, count, carry
  D_Flip_Flop x0 (.clk(_1), .D(dash), .Q(out_6));  // open: Qn, preset, en, reset
  D_Flip_Flop x1 (.clk(_1), .D(out_6), .Q(out_7));  // open: Qn, preset, en, reset
  D_Flip_Flop x2 (.clk(_1), .D(out_7), .Q(out_8));  // open: Qn, preset, en, reset
  D_Flip_Flop x3 (.clk(_1), .D(out_8), .Q(out_9));  // open: Qn, preset, en, reset
  Multiplexer #(.select(2)) multiplexer_1 (
    .in0(1'b0), .in1(1'b0), .in2(1'b1), .in3(1'b1), .out(multiplexer_1_out), .sel(counter_1_q));  // open: en
  Multiplexer #(.select(2)) multiplexer_2 (
    .in0(1'b0), .in1(1'b1), .in2(1'b0), .in3(1'b1), .out(multiplexer_2_out), .sel(counter_1_q));  // open: en
  D_Flip_Flop x4 (.clk(_1), .D(multiplexer_1_out), .Q(out_11));  // open: Qn, preset, en, reset
  D_Flip_Flop x6 (.clk(_1), .D(multiplexer_2_out), .Q(out_12));  // open: Qn, preset, en, reset

  // Notes on the sheet:
  //   morsekod till arduinon
endmodule

module Comparator (
  input  [3:0] in_1,
  input  [3:0] in_2,
  output out_3
);

  wire clock_1_out, comparator_1_gt, comparator_2_eq;
  wire [3:0] register_1_q;

  Clock clock_1 (.out(clock_1_out));
  Register #(.width(4)) register_1 (.D(in_1), .Q(register_1_q), .clk(clock_1_out));  // open: en, clr
  and and_1 (out_3, comparator_1_gt, comparator_2_eq);
  Comparator_part #(.width(4)) comparator_1 (.a(register_1_q), .b(4'b0110), .gt(comparator_1_gt));  // open: eq, lt
  Comparator_part #(.width(4)) comparator_2 (.a(4'b0001), .b(in_2), .eq(comparator_2_eq));  // open: gt, lt
endmodule
