// Logisim project Morseavkodare.circ as structural Verilog: 16 circuits, main circuit Knapptrycksräknare
module \Knapptrycksräknare  (
  input  in_1,
  output [3:0] out_2,
  output [3:0] out_3
);

  wire clock_1_out, not_1_out;

  Clock clock_1 (.out(clock_1_out));
  Counter #(.width(4), .max('hf), .ongoal("stay")) counter_1 (
    .count(not_1_out), .Q(out_2), .clk(clock_1_out), .clr(in_1));  // open: load, D, carry
  not not_1 (not_1_out, in_1);
  Counter #(.width(4), .max('hf), .ongoal("stay")) counter_2 (
    .count(in_1), .Q(out_3), .clk(clock_1_out), .clr(not_1_out));  // open: load, D, carry
endmodule

module \Räknare_och_avkodare_tillsammans  (
  input  in_1,
  output dash,
  output _7,
  output _3,
  output _1,
  output dot
);

  wire [3:0] \knapptrycksräknare_med_stay_at_value_1_out_2 , \knapptrycksräknare_med_stay_at_value_1_out_3 ;

  Clock clock_1 ();  // open: out
  Pausavkodare pausavkodare_1 (
    .out_2(_7), .\mellan_bokstäver (_3), .out_4(_1), .in_1(\knapptrycksräknare_med_stay_at_value_1_out_2 ));
  \Knapptrycksräknare_med_stay_at_value  \knapptrycksräknare_med_stay_at_value_1  (
    .in_1(in_1), .out_2(\knapptrycksräknare_med_stay_at_value_1_out_2 ),
    .out_3(\knapptrycksräknare_med_stay_at_value_1_out_3 ));
  Knapptrycksavkodare knapptrycksavkodare_1 (
    .dash(dash), .dot(dot), .in_1(\knapptrycksräknare_med_stay_at_value_1_out_3 ));
endmodule

module Knapptrycksavkodare (
  input  [3:0] in_1,
  output dot,
  output dash
);

  wire clock_1_out, komparator_konstant_0_1_out_2, komparator_konstant_0_2_out_2,
       komparator_konstant_2_1_x_2, komparator_konstant_2_1_x_2_2, not_1_out, xor_1_out;
  wire [3:0] register_1_q;

  Clock clock_1 (.out(clock_1_out));
  xor xor_1 (xor_1_out, clock_1_out, in_1[0]);
  Register #(.width(4)) register_1 (.D(in_1), .Q(register_1_q), .clk(xor_1_out));  // open: en, clr
  and and_1 (dash, komparator_konstant_2_1_x_2_2, komparator_konstant_0_1_out_2);
  Komparator__konstant__2 komparator_konstant_2_1 (
    .in_1(register_1_q), .X_2(komparator_konstant_2_1_x_2), .X_2_2(komparator_konstant_2_1_x_2_2));
  Komparator__konstant__0 komparator_konstant_0_1 (.in_1(in_1), .out_2(komparator_konstant_0_1_out_2));
  Komparator__konstant__0 komparator_konstant_0_2 (.in_1(register_1_q), .out_2(komparator_konstant_0_2_out_2));
  and and_2 (dot, komparator_konstant_0_1_out_2, not_1_out, komparator_konstant_2_1_x_2);
  not not_1 (not_1_out, komparator_konstant_0_2_out_2);
  Counter counter_1 ();  // open: load, D, count, Q, carry, clk, clr
endmodule

module Pausavkodare (
  input  [3:0] in_1,
  output out_2,
  output \mellan_bokstäver ,
  output out_4
);

  wire clock_1_out, komparator_konstant_0_1_out_2, komparator_konstant_0_2_out_2,
       komparator_konstant_2_1_x_2, komparator_konstant_2_1_x_2_2, komparator_konstant_6_1_a_6,
       komparator_konstant_6_1_a_6_2, not_1_out, xor_1_out;
  wire [3:0] register_1_q;

  Clock clock_1 (.out(clock_1_out));
  xor xor_1 (xor_1_out, clock_1_out, in_1[0]);
  Komparator__konstant__6 komparator_konstant_6_1 (
    .in_1(register_1_q), .A_6(komparator_konstant_6_1_a_6), .A_6_2(komparator_konstant_6_1_a_6_2));
  Register #(.width(4)) register_1 (.D(in_1), .Q(register_1_q), .clk(xor_1_out));  // open: en, clr
  and and_1 (out_2, komparator_konstant_6_1_a_6, komparator_konstant_0_1_out_2);
  Komparator__konstant__2 komparator_konstant_2_1 (
    .in_1(register_1_q), .X_2(komparator_konstant_2_1_x_2), .X_2_2(komparator_konstant_2_1_x_2_2));
  Komparator__konstant__0 komparator_konstant_0_1 (.in_1(in_1), .out_2(komparator_konstant_0_1_out_2));
  and and_2 (\mellan_bokstäver , komparator_konstant_2_1_x_2_2, komparator_konstant_6_1_a_6_2, komparator_konstant_0_1_out_2);
  and and_3 (out_4, komparator_konstant_0_1_out_2, not_1_out, komparator_konstant_2_1_x_2);
  not not_1 (not_1_out, komparator_konstant_0_2_out_2);
  Komparator__konstant__0 komparator_konstant_0_2 (.in_1(register_1_q), .out_2(komparator_konstant_0_2_out_2));

  // Notes on the sheet:
  //   mellanslag
  //   mellan delar av en bokstav
endmodule

module Main (
  output x0_out,
  output x1_out,
  output x2_out,
  output x3_out,
  output Space,
  output x4_out,
  output Send,
  output c2_out,
  output c1_out,
  output c0__out
);

  wire and_1_out, button_1_out, clock_1_out, d_ff_1_q, d_ff_2_q, d_ff_3_q, komparator_konstant_5_1_x__5,
       multiplexer_1_out, multiplexer_2_out, multiplexer_3_out, not_1_out, or_2_out, or_4_out, or_5_out,
       or_6_out, \räknare_och_avkodare_tillsammans_1__1 , \räknare_och_avkodare_tillsammans_1__3 ,
       \räknare_och_avkodare_tillsammans_1__7 , \räknare_och_avkodare_tillsammans_1_dash ,
       \räknare_och_avkodare_tillsammans_1_dot ;
  wire [2:0] counter_1_q;

  or or_1 (Space, \räknare_och_avkodare_tillsammans_1__7 , komparator_konstant_5_1_x__5);
  or or_2 (or_2_out, \räknare_och_avkodare_tillsammans_1_dot , \räknare_och_avkodare_tillsammans_1_dash , \räknare_och_avkodare_tillsammans_1__1 , \räknare_och_avkodare_tillsammans_1__3 , \räknare_och_avkodare_tillsammans_1__7 );
  Button button_1 (.out(button_1_out));
  or or_3 (Send, \räknare_och_avkodare_tillsammans_1__7 , \räknare_och_avkodare_tillsammans_1__3 );
  \Räknare_och_avkodare_tillsammans  \räknare_och_avkodare_tillsammans_1  (
    .in_1(button_1_out), ._7(\räknare_och_avkodare_tillsammans_1__7 ),
    ._3(\räknare_och_avkodare_tillsammans_1__3 ), ._1(\räknare_och_avkodare_tillsammans_1__1 ),
    .dash(\räknare_och_avkodare_tillsammans_1_dash ), .dot(\räknare_och_avkodare_tillsammans_1_dot ));
  or or_4 (or_4_out, d_ff_1_q, \räknare_och_avkodare_tillsammans_1_dash );
  Clock clock_1 (.out(clock_1_out));
  D_Flip_Flop d_ff_1 (.clk(clock_1_out), .D(or_4_out), .Q(d_ff_1_q), .reset(or_5_out));  // open: Qn, preset, en
  or or_5 (or_5_out, Send, \räknare_och_avkodare_tillsammans_1__1 );
  D_Flip_Flop d_ff_2 (.clk(or_2_out), .D(Send), .Q(d_ff_2_q), .reset(or_6_out));  // open: Qn, preset, en
  not not_1 (not_1_out, d_ff_2_q);
  Counter #(.width(3), .max('h7)) counter_1 (
    .count(or_5_out), .Q(counter_1_q), .clk(clock_1_out), .clr(or_6_out));  // open: load, D, carry
  and and_1 (and_1_out, not_1_out, d_ff_3_q);
  D_Flip_Flop d_ff_3 (.clk(or_2_out), .D(d_ff_2_q), .Q(d_ff_3_q), .reset(or_6_out));  // open: Qn, preset, en
  Komparator__konstant____5 komparator_konstant_5_1 (.in_1(counter_1_q), .X__5(komparator_konstant_5_1_x__5));
  D_Flip_Flop x0 (.clk(or_5_out), .D(d_ff_1_q), .Q(x0_out), .reset(or_6_out));  // open: Qn, preset, en
  D_Flip_Flop x1 (.clk(or_5_out), .D(x0_out), .Q(x1_out), .reset(or_6_out));  // open: Qn, preset, en
  D_Flip_Flop x2 (.clk(or_5_out), .D(x1_out), .Q(x2_out), .reset(or_6_out));  // open: Qn, preset, en
  D_Flip_Flop x3 (.clk(or_5_out), .D(x2_out), .Q(x3_out), .reset(or_6_out));  // open: Qn, preset, en
  D_Flip_Flop x4 (.clk(or_5_out), .D(x3_out), .Q(x4_out), .reset(or_6_out));  // open: Qn, preset, en
  or or_6 (or_6_out, and_1_out, komparator_konstant_5_1_x__5);
  Multiplexer #(.select(3)) multiplexer_1 (
    .in0(1'b0), .in1(1'b0), .in2(1'b0), .in3(1'b0), .in4(1'b1), .in5(1'b1), .out(multiplexer_1_out),
    .sel(counter_1_q));  // open: in6, in7, en
  Multiplexer #(.select(3)) multiplexer_2 (
    .in0(1'b0), .in1(1'b0), .in2(1'b1), .in3(1'b1), .in4(1'b0), .out(multiplexer_2_out), .sel(counter_1_q));  // open: in5, in6, in7, en
  Multiplexer #(.select(3)) multiplexer_3 (
    .in0(1'b0), .in1(1'b1), .in2(1'b0), .in3(1'b1), .in4(1'b0), .out(multiplexer_3_out), .sel(counter_1_q));  // open: in5, in6, in7, en
  D_Flip_Flop c2 (.clk(or_5_out), .D(multiplexer_1_out), .Q(c2_out), .reset(or_6_out));  // open: Qn, preset, en
  D_Flip_Flop c1 (.clk(or_5_out), .D(multiplexer_2_out), .Q(c1_out), .reset(or_6_out));  // open: Qn, preset, en
  D_Flip_Flop c0 (.clk(or_5_out), .D(multiplexer_3_out), .Q(c0__out), .reset(or_6_out));  // open: Qn, preset, en

  // Notes on the sheet:
  //   morsekod till arduinon
endmodule

module Komparator (
  input  A0,
  input  A1,
  input  A2,
  input  A3,
  input  B0,
  input  B1,
  input  B2,
  input  B3,
  output A_B,
  output A_B_2,
  output A_B_3
);

  wire and_1_out, and_2_out, and_3_out, and_4_out, and_5_out, and_6_out, and_7_out, and_8_out, not_1_out,
       not_2_out, not_3_out, not_4_out, not_5_out, not_6_out, not_7_out, not_8_out, not_9_out, not_10_out,
       not_11_out, not_12_out, not_13_out, not_14_out, not_15_out, not_16_out, not_17_out, not_18_out,
       xor_1_out, xor_2_out, xor_3_out, xor_4_out;

  not not_1 (not_1_out, A0);
  and and_1 (and_1_out, A0, not_2_out);
  not not_2 (not_2_out, B0);
  not not_3 (not_3_out, and_1_out);
  not not_4 (not_4_out, B1);
  xor xor_1 (xor_1_out, A0, B0);
  xor xor_2 (xor_2_out, A1, B1);
  xor xor_3 (xor_3_out, A2, B2);
  xor xor_4 (xor_4_out, A3, B3);
  and and_2 (and_2_out, B0, not_1_out);
  not not_5 (not_5_out, and_2_out);
  and and_3 (and_3_out, B1, not_5_out, not_6_out);
  not not_6 (not_6_out, A1);
  and and_4 (and_4_out, A1, not_3_out, not_4_out);
  not not_7 (not_7_out, and_4_out);
  and and_5 (and_5_out, not_7_out, not_3_out, A2, not_8_out);
  not not_8 (not_8_out, B2);
  not not_9 (not_9_out, xor_1_out);
  not not_10 (not_10_out, xor_2_out);
  not not_11 (not_11_out, xor_3_out);
  not not_12 (not_12_out, xor_4_out);
  not not_13 (not_13_out, and_3_out);
  and and_6 (and_6_out, not_13_out, not_5_out, B2, not_14_out);
  not not_14 (not_14_out, A2);
  not not_15 (not_15_out, and_6_out);
  not not_16 (not_16_out, A3);
  not not_17 (not_17_out, and_5_out);
  and and_7 (and_7_out, not_17_out, not_7_out, not_3_out, A3, not_18_out);
  not not_18 (not_18_out, B3);
  and and_8 (and_8_out, not_15_out, not_13_out, not_5_out, B3, not_16_out);
  or or_1 (A_B, and_1_out, and_4_out, and_5_out, and_7_out);
  and and_9 (A_B_2, not_9_out, not_10_out, not_11_out, not_12_out);
  or or_2 (A_B_3, and_2_out, and_3_out, and_6_out, and_8_out);

  // Notes on the sheet:
  //   Input A
  //   Input B
endmodule

module Komparator__konstant__3 (
  input  [3:0] in_1,
  output A_3,
  output A_3_2
);

  wire not_1_out, not_2_out;

  not not_1 (not_1_out, in_1[3]);
  not not_2 (not_2_out, in_1[2]);
  or or_1 (A_3_2, in_1[3], in_1[2]);
  and and_1 (A_3, not_1_out, not_2_out);
endmodule

module Komparator__konstant__0 (
  input  [3:0] in_1,
  output out_2
);

  wire not_1_out, not_2_out, not_3_out, not_4_out;

  not not_1 (not_1_out, in_1[0]);
  not not_2 (not_2_out, in_1[1]);
  not not_3 (not_3_out, in_1[2]);
  not not_4 (not_4_out, in_1[3]);
  and and_1 (out_2, not_1_out, not_2_out, not_3_out, not_4_out);
endmodule

module Komparator__konstant__7 (
  input  [3:0] in_1,
  output A_7,
  output A_7_2
);

  not not_1 (A_7_2, in_1[3]);

  assign A_7 = in_1[3];
endmodule

module Komparator__konstant__2 (
  input  [3:0] in_1,
  output X_2,
  output X_2_2
);

  wire and_1_out, and_2_out, not_1_out, not_2_out, not_3_out, not_4_out;

  not not_1 (not_1_out, in_1[0]);
  not not_2 (not_2_out, in_1[2]);
  not not_3 (not_3_out, in_1[3]);
  and and_1 (and_1_out, not_1_out, in_1[1], not_2_out, not_3_out);
  not not_4 (not_4_out, in_1[1]);
  or or_1 (X_2, and_1_out, and_2_out);
  and and_2 (and_2_out, not_2_out, not_3_out, not_4_out);
  not not_5 (X_2_2, X_2);
endmodule

module \Knapptrycksräknare_med_stay_at_value  (
  input  in_1,
  output [3:0] out_2,
  output [3:0] out_3
);

  wire clock_1_out, counter_1_carry, counter_2_carry, d_ff_1_q, d_ff_2_q, not_1_out, or_1_out, or_2_out;
  wire [3:0] counter_1_q, counter_2_q;

  or or_1 (or_1_out, d_ff_1_q, counter_1_carry);
  Clock clock_1 (.out(clock_1_out));
  D_Flip_Flop d_ff_1 (.clk(clock_1_out), .D(or_1_out), .Q(d_ff_1_q), .reset(in_1));  // open: Qn, preset, en
  Counter #(.width(4), .max('hf)) counter_1 (
    .Q(counter_1_q), .carry(counter_1_carry), .clk(clock_1_out), .clr(in_1));  // open: load, D, count
  not not_1 (not_1_out, in_1);
  Multiplexer #(.width(4)) multiplexer_1 (.in0(counter_1_q), .in1(4'b1111), .out(out_2), .sel(d_ff_1_q));  // open: en
  Counter #(.width(4), .max('hf)) counter_2 (
    .Q(counter_2_q), .carry(counter_2_carry), .clk(clock_1_out), .clr(not_1_out));  // open: load, D, count
  or or_2 (or_2_out, d_ff_2_q, counter_2_carry);
  Multiplexer #(.width(4)) multiplexer_2 (.in0(counter_2_q), .in1(4'b1111), .out(out_3), .sel(d_ff_2_q));  // open: en
  D_Flip_Flop d_ff_2 (.clk(clock_1_out), .D(or_2_out), .Q(d_ff_2_q), .reset(not_1_out));  // open: Qn, preset, en
endmodule

module Komparator___konstant____15 (
  input  [3:0] in_1,
  output X__15
);

  and and_1 (X__15, in_1[0], in_1[1], in_1[2], in_1[3]);
endmodule

module Komparator__konstant__6 (
  input  [3:0] in_1,
  output A_6,
  output A_6_2
);

  wire nand_1_out, not_1_out;

  not not_1 (not_1_out, in_1[3]);
  nand nand_1 (nand_1_out, in_1[0], in_1[1], in_1[2]);
  and and_1 (A_6_2, nand_1_out, not_1_out);
  not not_2 (A_6, A_6_2);
endmodule

module Komparator__konstant____5 (
  input  [2:0] in_1,
  output X__5
);

  wire not_1_out;

  not not_1 (not_1_out, in_1[1]);
  and and_1 (X__5, in_1[0], not_1_out, in_1[2]);
endmodule

module Ny_main (
  output x0_out,
  output x1_out,
  output x2_out,
  output x3_out,
  output Space,
  output x4_out,
  output Send,
  output c2_out,
  output c1_out,
  output c0__out
);

  wire button_1_out, clock_1_out, d_ff_1_q, komparator_konstant_5_1_x__5, multiplexer_1_out,
       multiplexer_2_out, multiplexer_3_out, or_3_out, or_4_out, or_5_out,
       \räknare_och_avkodare_tillsammans_1__1 , \räknare_och_avkodare_tillsammans_1__3 ,
       \räknare_och_avkodare_tillsammans_1__7 , \räknare_och_avkodare_tillsammans_1_dash ;
  wire [2:0] counter_1_q;

  or or_1 (Space, \räknare_och_avkodare_tillsammans_1__7 , komparator_konstant_5_1_x__5);
  Button button_1 (.out(button_1_out));
  or or_2 (Send, \räknare_och_avkodare_tillsammans_1__7 , \räknare_och_avkodare_tillsammans_1__3 );
  \Räknare_och_avkodare_tillsammans  \räknare_och_avkodare_tillsammans_1  (
    .in_1(button_1_out), ._7(\räknare_och_avkodare_tillsammans_1__7 ),
    ._3(\räknare_och_avkodare_tillsammans_1__3 ), ._1(\räknare_och_avkodare_tillsammans_1__1 ),
    .dash(\räknare_och_avkodare_tillsammans_1_dash ));  // open: dot
  or or_3 (or_3_out, d_ff_1_q, \räknare_och_avkodare_tillsammans_1_dash );
  Clock clock_1 (.out(clock_1_out));
  D_Flip_Flop d_ff_1 (.clk(clock_1_out), .D(or_3_out), .Q(d_ff_1_q), .reset(or_4_out));  // open: Qn, preset, en
  or or_4 (or_4_out, Send, \räknare_och_avkodare_tillsammans_1__1 );
  Counter #(.width(3), .max('h7)) counter_1 (
    .count(\räknare_och_avkodare_tillsammans_1__1 ), .Q(counter_1_q), .clk(clock_1_out), .clr(or_5_out));  // open: load, D, carry
  Komparator__konstant____5 komparator_konstant_5_1 (.in_1(counter_1_q), .X__5(komparator_konstant_5_1_x__5));
  D_Flip_Flop x0 (.clk(or_4_out), .D(d_ff_1_q), .Q(x0_out));  // open: Qn, preset, en, reset
  D_Flip_Flop x1 (.clk(or_4_out), .D(x0_out), .Q(x1_out));  // open: Qn, preset, en, reset
  D_Flip_Flop x2 (.clk(or_4_out), .D(x1_out), .Q(x2_out));  // open: Qn, preset, en, reset
  D_Flip_Flop x3 (.clk(or_4_out), .D(x2_out), .Q(x3_out));  // open: Qn, preset, en, reset
  D_Flip_Flop x4 (.clk(or_4_out), .D(x3_out), .Q(x4_out));  // open: Qn, preset, en, reset
  or or_5 (or_5_out, komparator_konstant_5_1_x__5, Send);
  Multiplexer #(.select(3)) multiplexer_1 (
    .in0(1'b0), .in1(1'b0), .in2(1'b0), .in3(1'b0), .in4(1'b1), .in5(1'b1), .out(multiplexer_1_out),
    .sel(counter_1_q));  // open: in6, in7, en
  Multiplexer #(.select(3)) multiplexer_2 (
    .in0(1'b0), .in1(1'b0), .in2(1'b1), .in3(1'b1), .in4(1'b0), .out(multiplexer_2_out), .sel(counter_1_q));  // open: in5, in6, in7, en
  Multiplexer #(.select(3)) multiplexer_3 (
    .in0(1'b0), .in1(1'b1), .in2(1'b0), .in3(1'b1), .in4(1'b0), .out(multiplexer_3_out), .sel(counter_1_q));  // open: in5, in6, in7, en
  D_Flip_Flop c2 (.clk(or_4_out), .D(multiplexer_1_out), .Q(c2_out));  // open: Qn, preset, en, reset
  D_Flip_Flop c1 (.clk(or_4_out), .D(multiplexer_2_out), .Q(c1_out));  // open: Qn, preset, en, reset
  D_Flip_Flop c0 (.clk(or_4_out), .D(multiplexer_3_out), .Q(c0__out));  // open: Qn, preset, en, reset

  // Notes on the sheet:
  //   morsekod till arduinon
endmodule

module \Räknare_och_avk__utan_stay  (
  input  in_1,
  output dash,
  output _7,
  output _3,
  output _1,
  output dot
);

  wire [3:0] \knapptrycksräknare_med_stay_at_value_1_out_2 , \knapptrycksräknare_med_stay_at_value_1_out_3 ;

  Clock clock_1 ();  // open: out
  Pausavkodare pausavkodare_1 (
    .out_2(_7), .\mellan_bokstäver (_3), .out_4(_1), .in_1(\knapptrycksräknare_med_stay_at_value_1_out_2 ));
  \Knapptrycksräknare_med_stay_at_value  \knapptrycksräknare_med_stay_at_value_1  (
    .in_1(in_1), .out_2(\knapptrycksräknare_med_stay_at_value_1_out_2 ),
    .out_3(\knapptrycksräknare_med_stay_at_value_1_out_3 ));
  Knapptrycksavkodare knapptrycksavkodare_1 (
    .dash(dash), .dot(dot), .in_1(\knapptrycksräknare_med_stay_at_value_1_out_3 ));
endmodule
