// Logisim project Register-skiss.circ as structural Verilog: 1 circuit, main circuit main
module main (
);

  wire and_1_out, and_2_out, and_3_out, and_4_out, and_5_out, and_7_out, button_1_out, clock_1_out, d_ff_1_q,
       d_ff_2_q, d_ff_3_q, d_ff_4_q, d_ff_5_q, d_ff_6_q, d_ff_6_qn, not_1_out, not_2_out, not_3_out,
       not_4_out, undriven, undriven_2;

  not not_1 (not_1_out, button_1_out);
  Button button_1 (.out(button_1_out));
  Counter counter_1 (.D(8'h1), .clk(clock_1_out), .clr(and_5_out));  // open: load, count, Q, carry
  Clock clock_1 (.out(clock_1_out));
  and and_1 (and_1_out, not_1_out, d_ff_5_q);
  and and_2 (and_2_out, not_1_out, d_ff_6_q);
  D_Flip_Flop d_ff_1 (.clk(clock_1_out), .D(and_3_out), .Q(d_ff_1_q), .reset(and_5_out));  // open: Qn, preset, en
  and and_3 (and_3_out, button_1_out, d_ff_2_q);
  D_Flip_Flop d_ff_2 (.clk(clock_1_out), .D(and_4_out), .Q(d_ff_2_q), .reset(and_5_out));  // open: Qn, preset, en
  and and_4 (and_4_out, button_1_out, d_ff_3_q);
  D_Flip_Flop d_ff_3 (.clk(clock_1_out), .D(button_1_out), .Q(d_ff_3_q), .reset(and_5_out));  // open: Qn, preset, en
  not not_2 (not_2_out, button_1_out);
  D_Flip_Flop d_ff_4 (.clk(undriven), .D(and_1_out), .Q(d_ff_4_q), .reset(undriven_2));  // open: Qn, preset, en
  D_Flip_Flop d_ff_5 (.clk(undriven), .D(and_2_out), .Q(d_ff_5_q), .reset(undriven_2));  // open: Qn, preset, en
  D_Flip_Flop d_ff_6 (
    .clk(undriven), .D(not_1_out), .Q(d_ff_6_q), .Qn(d_ff_6_qn), .reset(undriven_2));  // open: preset, en
  and and_5 (and_5_out, not_2_out, d_ff_1_q);
  not not_3 (not_3_out, d_ff_2_q);
  not not_4 (not_4_out, d_ff_1_q);
  // AND_Gate and_6 is placed but not wired
  and and_7 (and_7_out, d_ff_3_q, not_3_out, not_4_out, not_2_out);
endmodule
